# Fritzing sketch Results (saved by Fritzing 0.9.3b)
breadboards: 1

parts:
  Part1 = Arduino Mega 2560 (Rev3)
  U1 = AD7745 [package=tssop16]
  U2 = AD7745 [package=tssop16]
  J1 = Basic Force Sensing Resistor (FSR) [package=THT]
  J2 = Basic Force Sensing Resistor (FSR) [package=THT]
  U3 = SUP500F [package=sup500f]
  SEN1 = Pulse Sensor [package=SIP-3]
  Part2 = InvenSense MPU6050

nets:
  N1: Part1.A15, SEN1.Signal
  N2: Part1.D52, Part2.SDA
  N3: Part1.D53, U3.TX-O
  GND: Part1.GND, U3.GND, Part2.SCL
  N4: U1.SCL, U1.SDA, U2.SCL, U2.SDA, J1.pin_0, J2.pin_1, U3.VBAT, U3.PPS, U3.PSEL
  N5: U1._RDY, U1.NC, U2._RDY, U2.NC
  N6: U1.REFIN+, U1.REFIN-, U1.CIN1-, U1.CIN1+
  N7: U1.CIN2+, U1.CIN2-, U1.VIN+, U1.VIN-
  N8: U2.REFIN+, U2.REFIN-, U2.CIN1-, U2.CIN1+
  N9: U2.CIN2+, U2.CIN2-, U2.VIN+, U2.VIN-
  GND_2: U3.RX-I, SEN1.GND, Part2.GND
  VCC: U3.VCC, SEN1.VCC, Part2.VCC

custom parts:
  Pulse Sensor: Pulse Sensor Optical Heart Beat Sensor
